# Fritzing sketch LaspelyArduino-Schematic (saved by Fritzing 0.8.7b)
breadboards: 1

parts:
  µDuino = Arduino Uno (Rev3)
  R1 = Resistor [tolerance=±5% resistance=220 package=THT]
  R2 = Resistor [tolerance=±5% resistance=220 package=THT]
  LETSGO_switch = SWITCH_SPDT [package=kps-1290]
  ON/OFF_switch = SWITCH-SPST-2 [package=switch-spst-vertical]
  R3 = Resistor [tolerance=±5% resistance=220 package=THT]
  ALIMENTATION = Battery block 9V

nets:
  LOAD pour l'afficheur: µDuino.D10_PWM/SS
  CLOCK pour l'afficheur: µDuino.D11_PWM/MOSI
  DATAIN pour l'afficheur: µDuino.D12/MISO
  N1: µDuino.D2, R1.Pin_0
  N2: µDuino.D3_PWM, R2.Pin_0
  N3: µDuino.D4, LETSGO_switch.P
  N4: µDuino.5V, LETSGO_switch.O
  GND: µDuino.GND, R1.Pin_1, R2.Pin_1, R3.Pin_1, ALIMENTATION.-
  N5: µDuino.VIN, ON/OFF_switch.P
  N6: LETSGO_switch.S, R3.Pin_0
  N7: ON/OFF_switch.O, ALIMENTATION.+
